# Fritzing sketch schematic (saved by Fritzing 0.9.4)
breadboards: 1

parts:
  Raspberry_Pi_1 = Raspberry Pi 3 [part_number=RPI-3-V1.2]
  RHT1 = Humidity and Temperature Sensor RHT03
  R1 = Resistor [tolerance=±5% resistance=10k package="0603 [SMD]"]

nets:
  3V3: Raspberry_Pi_1.3v3, RHT1.Vcc, R1.Pin_0
  N1: Raspberry_Pi_1.GPIO4, RHT1.Data-signal, R1.Pin_1
  N2: Raspberry_Pi_1.GND, RHT1.GND_2
